# Fritzing sketch wireing_smart_pot_lcd_only (saved by Fritzing 1.0.4)

parts:
  LCD1 = Waveshare 2.4in LCD display
  MCU1 = Raspberry Pi Zero 2 W

nets:
  N1: LCD1.pin_1, MCU1.pin_2, MCU1.pin_4
  N2: LCD1.pin2, MCU1.pin_6
  N3: LCD1.pin3, MCU1.pin_19
  N4: LCD1.pin4, MCU1.pin_23
  N5: LCD1.pin_5, MCU1.pin_24
  N6: LCD1.pin_6, MCU1.pin_22
  N7: LCD1.pin_7, MCU1.pin_13
  N8: LCD1.pin_8, MCU1.pin_1, MCU1.pin_17

custom parts:
  Waveshare 2.4in LCD display: This is a generic 1.8 tft spi lcd display available on ebay and others. 240×320, General 2.4inch LCD Display Module, 65K RGB.
  Raspberry Pi Zero 2 W: The Raspberry Pi Zero is half the size of a Model A+, with twice the utility. A tiny Raspberry Pi that’s affordable enough for any project! · 1Ghz, Single-core CPU · 512MB RAM · Mini HDMI and USB On-The-Go ports · Micro USB power · HAT-compatible 40-pin header. Jan 2018: In this version schematic has been changed so the pins match the GPIO connector. I.e. the left hand pins are all the pins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
