# Fritzing sketch wireing_smart_pot_sensors_only (saved by Fritzing 1.0.4)

parts:
  Part1 = Adafruit ADS1115 16Bit I2C ADC [part_number="Adafruit #1085"]
  DS1 = DS18B20 1-Wire Temperature Sensor [part_number=DS18B20]
  Part2 = Soil Moisture Sensor
  Mod1 = KY-018 Photoresistor Module [package="Breakout board"]
  MCU1 = Raspberry Pi Zero 2 W
  R1 = Resistor [tolerance=±5% resistance=4.7k package="0805 [SMD]"]  # not connected

nets:
  N1: Part1.AIN2, Mod1.S
  N2: Part1.AIN1, Part2.SIG
  N3: Part1.SDA, MCU1.pin_3
  N4: Part1.SCL, MCU1.pin_5
  GND: Part1.GND, DS1.GND, Part2.GND, Mod1.Vin, MCU1.pin_6, MCU1.pin_20
  VDD: Part1.VDD, DS1.VDD, Part2.VCC, Mod1.-, MCU1.pin_2, MCU1.pin_4
  N5: DS1.DQ, MCU1.pin_7

custom parts:
  Adafruit ADS1115 16Bit I2C ADC: For microcontrollers without an analog-to-digital converter or when you want a higher-precision ADC, the ADS1115 provides 16-bit precision at 860 samples/second over I2C. The chip can be configured as 4 single-ended input channels, or two differential channels. As a nice bonus, it even includes a programmable gain amplifier, up to x16, to help boost up smaller single/differential signals to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
  KY-018 Photoresistor Module: KY-018 Photoresistor module, used to measure light intensity. It can determine the presence or absence of light.
  Raspberry Pi Zero 2 W: The Raspberry Pi Zero is half the size of a Model A+, with twice the utility. A tiny Raspberry Pi that’s affordable enough for any project! · 1Ghz, Single-core CPU · 512MB RAM · Mini HDMI and USB On-The-Go ports · Micro USB power · HAT-compatible 40-pin header. Jan 2018: In this version schematic has been changed so the pins match the GPIO connector. I.e. the left hand pins are all the pins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
